// Logisim project washingMachinev2.4.circ as structural Verilog
module main (
  input  Input_1,
  input  Input_2,
  input  Input_3,
  input  [1:0] Input_bus_1,
  input  [1:0] Input_bus_2,
  input  Input_4,
  input  Input_5,
  input  [2:0] Input_bus_3,
  input  Input_6,
  output Output_1
);

  wire a1, a2, a3, b1, b2, b3, c1, c2, c3, clk, clock_1_out, d1, d2, d3, e1, e2, e3, enCentrifuga, enClatire,
       enClatireSupl, enPresp, enSpalare, enUsa, f1, f2, f3, g1, g2, g3, gtCentrifuga, gtClatire,
       gtClatireSupl, gtPresp, gtSpalare, gtUsa;
  wire [3:0] sute, unitati, zeci;
  wire [8:0] decodertime_1_outtimp, timpPrespalare, timpSpalare, unitateexecutie_1_elapsedtime;

  Clock clock_1 (.out(clock_1_out));
  _7_Segment_Display L_7_Segment_Display_1 (.g(g1), .f(f1), .a(a1), .b(b1), .e(e1), .d(d1), .c(c1), .dp(1'b0));
  _7_Segment_Display L_7_Segment_Display_2 (.g(g2), .f(f2), .a(a2), .b(b2), .e(e2), .d(d2), .c(c2), .dp(1'b0));
  _7_Segment_Display L_7_Segment_Display_3 (.g(g3), .f(f3), .a(a3), .b(b3), .e(e3), .d(d3), .c(c3), .dp(1'b0));
  DivizorFrecv divizorfrecv_1 (.clock(clock_1_out), .div_clk(clk));
  DecoderTime decodertime_1 (
    .inTemp(Input_bus_1), .enable(Input_1), .mode(Input_bus_3), .modSelectie(Input_6), .prespalare(Input_4),
    .clatireSuplimentara(Input_5), .outTimp(decodertime_1_outtimp));
  DecoderTemp decodertemp_1 (
    .inTemp(Input_bus_1), .enable(Input_1), .mode(Input_bus_3), .modSelectie(Input_6), .prespalare(Input_4),
    .outTimpSpalare(timpSpalare), .outTimpPrespalare(timpPrespalare));
  UnitateCentrala unitatecentrala_1 (
    .clock(clk), .start(Input_1), .usa(Input_2), .anulare(Input_3), .temperatura(Input_bus_1),
    .viteza(Input_bus_2), .prespalare(Input_4), .clatireSuplimentara(Input_5), .mode(Input_bus_3),
    .modSelectie(Input_6), .gtPrespalare(gtPresp), .gtSpalare(gtSpalare), .gtClatire(gtClatire),
    .gtClatireSuplimentara(gtClatireSupl), .gtCentrifuga(gtCentrifuga), .enPrespalare(enPresp),
    .enSpalare(enSpalare), .enClatire(enClatire), .enClatireSuplimentara(enClatireSupl),
    .enCentrifuga(enCentrifuga), .gataSpalare(Output_1));
  UnitateExecutie unitateexecutie_1 (
    .clk(clk), .\time (decodertime_1_outtimp), .timeSpalare(timpSpalare), .timePrespalare(timpPrespalare),
    .start(Input_1), .usa(Input_2), .anulare(Input_3), .enPrespalare(enPresp), .enSpalare(enSpalare),
    .enClatire(enClatire), .enClatireSuplimentara(enClatireSupl), .enCentrifuga(enCentrifuga),
    .gataSpalare(Output_1), .gataUsa(gtUsa), .temperatura(Input_bus_1), .viteza(Input_bus_2),
    .prespalare(Input_4), .clatireSuplimentara(Input_5), .mode(Input_bus_3), .modSelectie(Input_6),
    .elapsedTime(unitateexecutie_1_elapsedtime), .gtPrespalare(gtPresp), .gtSpalare(gtSpalare),
    .gtClatire(gtClatire), .gtClatireSuplimentara(gtClatireSupl), .gtCentrifuga(gtCentrifuga), .enT60(enUsa));
  Timer60 timer60_1 (.clk(clk), .enable(enUsa), .TC(gtUsa));
  BitsToSZU bitstoszu_1 (.\input (unitateexecutie_1_elapsedtime), .sute(sute), .zeci(zeci), .unitati(unitati));
  SegFault segfault_1 (.intrare(sute), .iesire({g1, f1, e1, d1, c1, b1, a1}));
  SegFault segfault_2 (.intrare(zeci), .iesire({g2, f2, e2, d2, c2, b2, a2}));
  SegFault segfault_3 (.intrare(unitati), .iesire({g3, f3, e3, d3, c3, b3, a3}));

  // Other names for the same wires on the sheet: an = Input_3; clatS = Input_5; en = Input_1; gataS = Output_1;
  //   mode[2:0] = Input_bus_3; modS = Input_6; presp = Input_4; temp[1:0] = Input_bus_1; usa = Input_2;
  //   vit[1:0] = Input_bus_2
endmodule

// VHDL entity UnitateCentrala, as the project stores it:
LIBRARY ieee;
USE ieee.std_logic_1164.all;
USE ieee.std_logic_unsigned.all;
USE ieee.numeric_std.all;

ENTITY UnitateCentrala IS
  PORT (
  	-- intrari ale UC
  	clock, start, usa, anulare: in std_logic;
  	temperatura: in std_logic_vector(1 downto 0);
  	viteza: in std_logic_vector(1 downto 0);
  	prespalare: in std_logic;
  	clatireSuplimentara: in std_logic;
  	mode: in std_logic_vector (2 downto 0);
	modSelectie: in std_logic;
	-- iesiri de la UC pentru UE
 	enPrespalare, enSpalare, enClatire, enClatireSuplimentara, enCentrifuga: out std_logic;
	-- iesiri de la UE pentru UC
 	gtPrespalare, gtSpalare, gtClatire, gtClatireSuplimentara, gtCentrifuga: in std_logic;

 	--iesire UC
 	gataSpalare: out std_logic
    );
END UnitateCentrala;

ARCHITECTURE turaDeSpalat OF UnitateCentrala IS

type State_T is (A_Idle, B_Prespalare, B_Spalare, C_Clatire, C_ClatireSuplimentara, D_Centrifuga, E_Gata);
signal State, nextState: State_T;
signal vitezaSelectata, rot: integer :=0;
signal spalare2, clatire2: integer :=0;
signal gata: integer :=0;

-- A -> idle, setari predefinite, setari manuale
-- B -> spalare/prespalare
-- C -> clatire
-- D -> centrifuga
-- E -> gata

-- moduri de spalare
-- 000 - spalare rapida
-- 001 - camasi
-- 010 - culori inchise
-- 011 - rufe murdare
-- 100 - antialergic

-- temperatura
-- 00 - 30
-- 01 - 40
-- 10 - 60
-- 11 - 90

-- modSelectie
-- 0, manual
-- 1, automat

BEGIN

-- dam update la stare
Update: process(clock, anulare)
		begin
			if(anulare = '1') then
				State <= A_Idle;
			elsif (rising_edge(clock)) then
				State <= NextState;
			end if;
		end process Update;

-- vezi organigrama
Transitions: process(start, anulare, usa, viteza, mode, modSelectie, prespalare, spalare2, clatireSuplimentara, clatire2, State, gtPrespalare, gtSpalare, gtClatire, gtClatireSuplimentara, gtCentrifuga)
			begin
				if(anulare = '1') then nextState <= A_Idle;
				else
				case State is
					when A_Idle =>
					if(start = '1' and usa= '1' and (prespalare = '1' or spalare2 = 1)) then nextState <= B_Prespalare;
					elsif (start ='1' and usa = '1' and (prespalare = '0' or spalare2 = 0)) then nextState <= B_Spalare;
					else nextState <= A_Idle;
					end if;

					when B_Prespalare =>
					if(gtPrespalare = '1') then nextState <= B_Spalare;
					else nextState <= B_Prespalare;
					end if;

					when B_Spalare =>
					if(gtSpalare = '1') then nextState <= C_Clatire;
					else nextState <= B_Spalare;
					end if;
					
					when C_Clatire =>
					if(gtClatire = '1' and (clatireSuplimentara = '1' or clatire2 = 1)) then nextState <= C_ClatireSuplimentara;
					elsif(gtClatire = '1' and (clatireSuplimentara = '0' or clatire2 = 0)) then nextState <= D_Centrifuga;
					else nextState<=C_Clatire;
					end if;

					when C_ClatireSuplimentara =>
					if(gtClatireSuplimentara = '1') then nextState <= D_Centrifuga;
					else nextState <= C_ClatireSuplimentara;
					end if;
					
					when D_Centrifuga =>
					if(gtCentrifuga = '1') then nextState <= E_Gata;
					else nextState <= D_Centrifuga;
					end if;

					when E_Gata =>
					nextState <= A_Idle;
				end case;
				end if;
			end process Transitions;

-- vezi relatii UC-UE
Outputs: process(start, anulare, viteza, usa, mode, modSelectie, prespalare, spalare2, clatireSuplimentara, clatire2, State, gtPrespalare, gtSpalare, gtClatire, gtClatireSuplimentara, gtCentrifuga)
		begin
			case State is
				when A_Idle =>
				vitezaSelectata <= 0; rot <= 0;
				enPrespalare<='0'; enSpalare<='0'; enClatire <='0'; enClatireSuplimentara<='0'; enCentrifuga<='0';
				if(gata = 0 or anulare = '1') then 
					gataSpalare <= '0'; gata <= 0;
					spalare2 <= 0; clatire2 <= 0;
				end if;
				
				if(modSelectie = '1') then
					if(to_integer(unsigned(mode)) = 0) then vitezaSelectata <= 1200;
					elsif(to_integer(unsigned(mode)) = 1) then vitezaSelectata <= 800;
					elsif(to_integer(unsigned(mode)) = 2) then vitezaSelectata <= 1000; clatire2 <= 1;
					elsif(to_integer(unsigned(mode)) = 3) then vitezaSelectata <= 1000; spalare2 <= 1;
					elsif(to_integer(unsigned(mode)) = 4) then vitezaSelectata <= 1200; clatire2 <= 1;
					end if;
				else
					if(viteza = 0) then vitezaSelectata <= 800;
					elsif(viteza = 1) then vitezaSelectata <= 1000;
					elsif(viteza = 2) then vitezaSelectata <= 1200;
					end if;
				end if;
	
				when B_Prespalare =>
				if(prespalare = '1' or spalare2 = 1) then
					enPrespalare <= '1'; rot <= 60;
				end if;

				when B_Spalare =>
				if(gata = 0) then enSpalare<='1'; rot <= 60; end if;
				
				when C_Clatire =>
				if(gata = 0) then enClatire <= '1'; rot <= 120; end if; -- enClatire

				when C_ClatireSuplimentara =>
				if(clatireSuplimentara = '1' or clatire2 = 1) then 
					if(gata = 0) then enClatireSuplimentara <= '1'; rot <= 120; end if; -- enClatireSuplimentara
				end if;
	
				when D_Centrifuga =>
				if(gata = 0) then enCentrifuga <= '1'; rot <= vitezaSelectata; end if;
			
				when E_Gata =>
				if(gata = 0) then gataSpalare <= '1'; gata <= 1; rot <= 0; end if;
			end case;
		end process Outputs;

END turaDeSpalat;

// VHDL entity UnitateExecutie, as the project stores it:
LIBRARY ieee;
USE ieee.std_logic_1164.all;
USE ieee.std_logic_unsigned.all;
USE ieee.numeric_std.all;

ENTITY UnitateExecutie IS
  PORT (
  	clk: in std_logic;
  	time: in std_logic_vector(8 downto 0);
  	timeSpalare, timePrespalare: in std_logic_vector(8 downto 0);
  	start, usa, anulare: in std_logic;
  	enPrespalare, enSpalare, enClatire, enClatireSuplimentara, enCentrifuga, gataSpalare, gataUsa: in std_logic;
  	temperatura, viteza: in std_logic_vector(1 downto 0);
  	prespalare, clatireSuplimentara: in std_logic;
  	mode: in std_logic_vector(2 downto 0);
  	modSelectie: in std_logic;
  	
  	
  	elapsedTime: out std_logic_vector(8 downto 0);
  	gtPrespalare, gtSpalare, gtClatire, gtClatireSuplimentara, gtCentrifuga, enT60: out std_logic
    );
END UnitateExecutie;

-- instead of using 11 timers like in v1.0, I implemented one single timer that is similar to the CU
-- 5 variables to count all the washing stages
-- formula for time determined in DecoderTime
-- formula for spalare and prespalare determined in DecoderTemp

ARCHITECTURE TypeArchitecture OF UnitateExecutie IS

signal tempSel, vitSel, modeSel: integer:=0;
signal prespSel, clatSel, modSelSel: std_logic;
BEGIN

process(tempSel, vitSel, modeSel, modSelSel, prespSel, clatSel, clk, time, timeSpalare, timePrespalare, start, usa, anulare, enPrespalare, enSpalare, enClatire, enClatireSuplimentara, enCentrifuga, gataSpalare, gataUsa, prespalare, clatireSuplimentara, modSelectie, mode)

variable count: integer :=0;
variable stop: integer :=0;
variable started: integer :=0;
variable countPrespalare, countSpalare, countClatire, countClatireSuplimentara, countCentrifuga: integer :=0;

begin
if(rising_edge(clk)) then
	tempSel <= to_integer(unsigned(temperatura));
	vitSel <= to_integer(unsigned(viteza));
	modeSel <= to_integer(unsigned(mode));
	prespSel <= prespalare;
	clatSel <= clatireSuplimentara;
	modSelSel <= modSelectie;

	if(vitSel = 3) then
		count:=-1; stop:=0;
		countPrespalare:=0; countSpalare:=0; countClatire:=0; countClatireSuplimentara:=0; countCentrifuga:=0;
		gtPrespalare<='0'; gtSpalare<='0'; gtClatire<='0'; gtClatireSuplimentara<='0'; gtCentrifuga<='0'; enT60 <= '0';
	end if;
	
	if(anulare = '1' or gataSpalare = '1' or start = '0' or usa = '0') then
		count:=0; stop:=0;
		countPrespalare:=0; countSpalare:=0; countClatire:=0; countClatireSuplimentara:=0; countCentrifuga:=0;
		gtPrespalare<='0'; gtSpalare<='0'; gtClatire<='0'; gtClatireSuplimentara<='0'; gtCentrifuga<='0'; enT60 <= '0';
	end if;
	if(start = '1' and usa = '1') then
		if(count > 0) then
			if(tempSel /= temperatura or vitSel /= viteza or modeSel /= mode or
			   prespSel /= prespalare or clatSel /= clatireSuplimentara or modSelSel /= modSelectie) then
			   count:=-2; stop:=0;
			   countPrespalare:=0; countSpalare:=0; countClatire:=0; countClatireSuplimentara:=0; countCentrifuga:=0;
		        gtPrespalare<='0'; gtSpalare<='0'; gtClatire<='0'; gtClatireSuplimentara<='0'; gtCentrifuga<='0'; enT60 <= '0';
			end if;
		end if;
		if(count = to_integer(unsigned(time)) and stop = 0) then
			enT60 <= '1';
			if(gataUsa = '1') then gtCentrifuga <= '1'; stop :=1;
			end if;
		elsif(stop = 0) then
			if(enPrespalare = '1') then 
				if(countPrespalare = timePrespalare) then gtPrespalare <= '1';
				elsif(gataSpalare = '0' and anulare = '0') then countPrespalare := countPrespalare + 1; count := count + 1;
				end if;
			end if;
			if(enSpalare = '1') then 
				if(countSpalare = timeSpalare) then gtSpalare <= '1'; 
				elsif(gataSpalare = '0' and anulare = '0') then  countSpalare := countSpalare + 1; count := count + 1;
				end if; 
			end if;
			if(enClatire = '1') then 
				if(countClatire = 10) then gtClatire <='1';
				elsif(gataSpalare = '0' and anulare = '0') then  countClatire := countClatire + 1; count := count + 1;
				end if; 
			end if;
			if(enClatireSuplimentara = '1') then
				if(countClatireSuplimentara = 10) then gtClatireSuplimentara <= '1';
				elsif(gataSpalare = '0' and anulare = '0') then  countClatireSuplimentara := countClatireSuplimentara + 1; count := count + 1;
				end if;
			end if;
			if(enCentrifuga = '1') then
				if(gataSpalare = '0' and anulare = '0') then  countCentrifuga := countCentrifuga + 1; count := count + 1;
				end if;
			end if; 
		end if;
	end if;
end if;
	if(stop = 1 or gataSpalare = '1') then elapsedTime <= "000000000";
	else elapsedTime <= std_logic_vector(to_unsigned(to_integer(unsigned(time))-count, elapsedTime'length));
	end if;
end process;

END TypeArchitecture;

// VHDL entity DecoderTime, as the project stores it:
LIBRARY ieee;
USE ieee.std_logic_1164.all;
USE ieee.std_logic_unsigned.all;
USE ieee.numeric_std.all;

ENTITY DecoderTime IS
  PORT (
  	inTemp: in std_logic_vector(1 downto 0);
  	enable: in std_logic;
  	mode: in std_logic_vector(2 downto 0);
  	modSelectie: in std_logic;
	prespalare: in std_logic;
	clatireSuplimentara: in std_logic;

  	outTimp: out std_logic_vector(8 downto 0)
    );
END DecoderTime;

--temperatura
--00 - 30
--01 - 40
--10 - 60
--11 - 90

-- decodificator care calculeaza timpul unui ciclu de spalare in functie de temperatura
-- util pt TimerK

ARCHITECTURE TypeArchitecture OF DecoderTime IS

BEGIN

-- Timp spalare: 2 * inTemp - 10 + (2 * inTemp - 20, if prespalare) +10 (+10, if clatireSuplimentara) + 10

-- Timp total normal: 2 * inTemp + 10
-- Timp total prespalare, nu clatire: 4 * inTemp - 10
-- Timp total nu prespalare, clatire: 2 * inTemp +20
-- Timp total prespalare, clatire: 4 * inTemp

--0, manual
--1, automat

process(inTemp, enable, mode, modSelectie, prespalare, clatireSuplimentara)
begin
	if(enable = '1' and modSelectie ='0') then
		case inTemp is
		when "00" => --temp 30
		if(prespalare = '0' and clatireSuplimentara = '0') then outTimp <="001000110";
		elsif(prespalare = '1' and clatireSuplimentara = '0') then outTimp <="001101110";
		elsif(prespalare = '0' and clatireSuplimentara = '1') then outTimp <="001010000";
		elsif(prespalare = '1' and clatireSuplimentara = '1') then outTimp <="001111000";
		end if;
		
		when "01" => -- temp 40
		if(prespalare = '0' and clatireSuplimentara = '0') then outTimp <="001011010";
		elsif(prespalare = '1' and clatireSuplimentara = '0') then outTimp <="010010110";
		elsif(prespalare = '0' and clatireSuplimentara = '1') then outTimp <="001100100";
		elsif(prespalare = '1' and clatireSuplimentara = '1') then outTimp <="010100000";
		end if;
		
		when "10" => -- temp 60
		if(prespalare = '0' and clatireSuplimentara = '0') then outTimp <="010000010";
		elsif(prespalare = '1' and clatireSuplimentara = '0') then outTimp <="011100110";
		elsif(prespalare = '0' and clatireSuplimentara = '1') then outTimp <="010001100";
		elsif(prespalare = '1' and clatireSuplimentara = '1') then outTimp <="011110000";
		end if;
		
		when "11" => -- temp 90
		if(prespalare = '0' and clatireSuplimentara = '0') then outTimp <="010111110";
		elsif(prespalare = '1' and clatireSuplimentara = '0') then outTimp <="101011110";
		elsif(prespalare = '0' and clatireSuplimentara = '1') then outTimp <="011001000";
		elsif(prespalare = '1' and clatireSuplimentara = '1') then outTimp <="101101000";
		end if;
		
		when others => outTimp<="000000000";
		end case;
	elsif(enable = '1' and modSelectie = '1') then
		case mode is
		when "000" => outTimp<="001000110"; -- temp 30
		when "001" => outTimp<="010000010"; -- temp 60
		when "010" => outTimp<="001100100"; -- temp 40, clatireSupl
		when "011" => outTimp<="010010110"; -- temp 40, prespalare
		when "100" => outTimp<="011001000"; -- temp 90, clatireSupl
		when others => outTimp<="000000000";
		end case;
	end if;
end process;

END TypeArchitecture;

// VHDL entity DecoderTemp, as the project stores it:
LIBRARY ieee;
USE ieee.std_logic_1164.all;
USE ieee.std_logic_unsigned.all;
USE ieee.numeric_std.all;

ENTITY DecoderTemp IS
  PORT (
  	inTemp: in std_logic_vector(1 downto 0);
  	enable: in std_logic;
  	mode: in std_logic_vector(2 downto 0);
  	modSelectie: in std_logic;
  	prespalare: in std_logic;

  	outTimpSpalare: out std_logic_vector(8 downto 0);
  	outTimpPrespalare: out std_logic_vector(8 downto 0)
    );
END DecoderTemp;

-- Calculates the time for spalare and prespalare using formula spalare and formula prespalare
-- Formula spalare : 2 * inTemp - 10 for spalare
-- Formula prespalare : 2 * inTemp - 20 for prespalare
-- util for TimerK

--temperatura
--00 - 30
--01 - 40
--10 - 60
--11 - 90

--0, mod manual
--1, mod automat

ARCHITECTURE TypeArchitecture of DecoderTemp is

BEGIN

process(inTemp, enable, mode, modSelectie, prespalare)
begin
	if(enable = '1' and modSelectie ='0') then
		case inTemp is
		when "00" => --temp 30
		outTimpSpalare <="000110010";
		outTimpPrespalare<="111111111"; 
		if(prespalare = '1') then outTimpPrespalare <="000101000"; end if;
		
		when "01" => -- temp 40
		outTimpSpalare <="001000110";
		outTimpPrespalare<="111111111"; 
		if(prespalare = '1') then outTimpPrespalare <="000111100"; end if; 
		
		when "10" => -- temp 60
		outTimpSpalare <="001101110";
		outTimpPrespalare<="111111111";
		if(prespalare = '1') then outTimpPrespalare <="001100100"; end if;
		
		when "11" => -- temp 90
		outTimpSpalare <="010101010";
		outTimpPrespalare<="111111111";
		if(prespalare = '1') then outTimpPrespalare <="010100000"; end if;
		
		when others => outTimpSpalare<="111111111"; outTimpPrespalare<="111111111";
		end case;
	elsif(enable = '1' and modSelectie = '1') then
		case mode is
		when "000" => outTimpSpalare <="000110010"; outTimpPrespalare<="111111111";-- temp 30
		when "001" => outTimpSpalare <="001101110"; outTimpPrespalare<="111111111";-- temp 60
		when "010" => outTimpSpalare <="001000110"; outTimpPrespalare<="111111111";-- temp 40, clatireSupl
		when "011" => outTimpSpalare <="001000110"; outTimpPrespalare <="000111100"; -- temp 40, prespalare
		when "100" => outTimpSpalare<="011001000"; outTimpPrespalare<="111111111";-- temp 90, clatireSupl
		when others => outTimpSpalare<="111111111"; outTimpPrespalare<="111111111";
		end case;
	end if;
end process;

END TypeArchitecture;

// VHDL entity BitsToSZU, as the project stores it:
LIBRARY ieee;
USE ieee.std_logic_1164.all;
USE ieee.std_logic_unsigned.all;
USE ieee.numeric_std.all;

ENTITY BitsToSZU IS
  PORT (
  	input: in std_logic_vector(8 downto 0);
  	sute, zeci, unitati : out std_logic_vector(3 downto 0)
    );
END BitsToSZU;

-- transforma un nr pe 9 biti in unitati, zeci si sute
-- util pt 7 seg

ARCHITECTURE TypeArchitecture OF BitsToSZU IS

BEGIN

process(input)

variable nr, a, b, c: integer:=0;

begin
	nr := to_integer(unsigned(input));
	a := nr/100; b:= (nr/10) mod 10; c:= nr mod 10;

	case a is
		when 0 => sute <= "0000";
		when 1 => sute <= "0001";
		when 2 => sute <= "0010";
		when 3 => sute <= "0011";
		when 4 => sute <= "0100";
		when 5 => sute <= "0101";
		when 6 => sute <= "0110";
		when 7 => sute <= "0111";
		when 8 => sute <= "1000";
		when 9 => sute <= "1001";
		when others => sute <= "1111";
	end case;

	case b is
		when 0 => zeci <= "0000";
		when 1 => zeci <= "0001";
		when 2 => zeci <= "0010";
		when 3 => zeci <= "0011";
		when 4 => zeci <= "0100";
		when 5 => zeci <= "0101";
		when 6 => zeci <= "0110";
		when 7 => zeci <= "0111";
		when 8 => zeci <= "1000";
		when 9 => zeci <= "1001";
		when others => zeci <= "1111";
	end case;

	case c is
		when 0 => unitati <= "0000";
		when 1 => unitati <= "0001";
		when 2 => unitati <= "0010";
		when 3 => unitati <= "0011";
		when 4 => unitati <= "0100";
		when 5 => unitati <= "0101";
		when 6 => unitati <= "0110";
		when 7 => unitati <= "0111";
		when 8 => unitati <= "1000";
		when 9 => unitati <= "1001";
		when others => unitati <= "1111";
	end case;
	
end process;

END TypeArchitecture;

// VHDL entity SegFault, as the project stores it:
LIBRARY ieee;
USE ieee.std_logic_1164.all;
USE ieee.std_logic_unsigned.all;
USE ieee.numeric_std.all;

ENTITY SegFault IS
  PORT (
  	intrare:in std_logic_vector(3 downto 0);
  	iesire:out std_logic_vector(6 downto 0)
    );
END SegFault;

-- 4 biti in 7 biti (gfedcba)

ARCHITECTURE TypeArchitecture OF SegFault IS

BEGIN

process(intrare)
begin
	case intrare is
		when "0000" => iesire <= "0111111";
		when "0001" => iesire <= "0000110";
		when "0010" => iesire <= "1011011";
		when "0011" => iesire <= "1001111";
		when "0100" => iesire <= "1100110";
		when "0101" => iesire <= "1101101";
		when "0110" => iesire <= "1111101";
		when "0111" => iesire <= "0000111";
		when "1000" => iesire <= "1111111";
		when "1001" => iesire <= "1101111";
		when others => iesire <= "1111111";
	end case;
end process;

END TypeArchitecture;

// VHDL entity DivizorFrecv, as the project stores it:
--------------------------------------------------------------------------------
-- Project :
-- File    :
-- Autor   :
-- Date    :
--
--------------------------------------------------------------------------------
-- Description :
--
--------------------------------------------------------------------------------

LIBRARY ieee;
USE ieee.std_logic_1164.all;
USE ieee.std_logic_unsigned.all;


ENTITY DivizorFrecv IS
					
  PORT (
  --Insert input ports below
 					-- numar ciclu				 0   1   2   3   4   5          49                 98   99  0   1   2
    clock      : IN  std_logic;                    -- tactul la 100 Mhz de ex. _|`\_|`\_|`\_|`\_|`\_|`\........_|`\_.............._|`\_|`\_|`\_|`\_|`\
    div_clk    : out std_logic				-- ceas divizat cu 100        __________________________________|``````````````````````\___________
    );
END DivizorFrecv;

--sa fie un numarator, si sa se afiseze pe 7 segment valorile/iesirile => va numara la frecventa clockului din placuta 100Hz => 
--------------------------------------------------------------------------------
--divizor de frecventa de la 100 Mhz la 1 Mhz de ex.

ARCHITECTURE TypeArchitecture OF DivizorFrecv IS

signal tmp:std_logic_vector (6 downto 0):=(others =>'0');--"0000000"
BEGIN

process (clock)
begin
	if (rising_edge(clock)) then
		if tmp = ("1100011") then tmp <="0000000";     -- verificam daca am ajuns la al 99'lea ciclu
		elsif (tmp <= "0110001") then 		-- -- verificam daca am ajuns la al 49'lea ciclu
			tmp <= tmp + 1;  -- timp de 50 de cicluri clock-ul divizat e '0'
			div_clk <= '0';
		else  div_clk <= '1';				-- timp de 50 de cicluri clock-ul divizat e '1'
			tmp <= tmp + 1;
	end if;
	end if;
end process;

END TypeArchitecture;

// VHDL entity Timer60, as the project stores it:
LIBRARY ieee;
USE ieee.std_logic_1164.all;
USE ieee.std_logic_unsigned.all;
USE ieee.numeric_std.all;

ENTITY Timer60 IS
  PORT (
  	clk: in std_logic;
  	enable: in std_logic;
  	
  	TC: out std_logic
    );
END Timer60;

ARCHITECTURE TypeArchitecture OF Timer60 IS

BEGIN
process(clk, enable)

variable count: integer :=0;

begin

if(rising_edge(clk)) then
	if(enable = '1') then
		if(count = 60) then
			count :=0;
			TC <= '1';
		else
			count := count+1;
			TC <= '0';
		end if;
	else
		count := 0;
		TC <= '0';
	end if;
end if;
	
end process;

END TypeArchitecture;
